# Fritzing sketch PWM controlled DC (saved by Fritzing 0.9.2b)
circuit board: 8.46667cm x 5.64444cm
breadboards: 1

parts:
  Часть1 = Arduino Uno (Rev3)
  Q1 = Basic FET N-Channel [part_number="K3918 KSGG" package="TO220 [THT]"]
  R1 = Resistor [tolerance=±5% resistance=1.35k package=THT]
  R2 = Resistor [tolerance=±5% resistance=24k package=THT]
  M1 = DC Motor
  Power_plug1 = Power plug

nets:
  N1: Часть1.D9_PWM, R1.Pin_0
  GND: Часть1.GND, Q1.source, R2.Pin_1, Power_plug1.GND
  N2: Q1.gate, R1.Pin_1, R2.Pin_0
  N3: Q1.drain, M1.pin_1
  N4: M1.pin_2, Power_plug1.VCC

// code stored in the sketch: PWMcontrolledDrive.ino
 int x = 128;
 
void setup() {
  // put your setup code here, to run once:
 
  
}

void loop() {
  // put your main code here, to run repeatedly:
  if (x < 255) 
  {
    x = x +1;
  }
  else
  {
    x = 128;
  }
  analogWrite(9, x);
  delay(500);
}
